// Logisim project CPU.circ as structural Verilog: 3 circuits, main circuit main
module main (
  input  in_1,
  output Signed_OverFlow,
  output equal
);

  wire clock_1_out, clock_2_out, MemWr, RegDst, RegWr;
  wire [4:0] decode_1_out_7, decode_1_rr1, decode_1_rr2, multiplexer_1_out;
  wire [5:0] decode_1_func, func;
  wire [15:0] decode_1_out_5;
  wire [23:0] instruction_memory_1_address, memory_data_1_address_2, memory_data_temp_1_address;
  wire [31:0] alu_1_result, instruction_memory_1_instruction, memory_data_temp_1_instruction,
       program_counter_1_pc, regfile_1_read_data1, regfile_1_read_data2, sign_extend_1_out_2;

  program_counter program_counter_1 (.PC(program_counter_1_pc), .clk(in_1));
  // Probe on program_counter_1_pc
  // Probe on instruction_memory_1_address
  instruction_memory instruction_memory_1 (
    .instruction(instruction_memory_1_instruction), .fetch_addr(program_counter_1_pc),
    .address(instruction_memory_1_address));
  // Probe on instruction_memory_1_instruction
  // Probe on decode_1_func
  Decode decode_1 (
    .Instruction(instruction_memory_1_instruction), .opcode(func), .RR1(decode_1_rr1), .RR2(decode_1_rr2),
    .out_5(decode_1_out_5), .func(decode_1_func), .out_7(decode_1_out_7));
  // Probe on decode_1_out_5
  // Probe on decode_1_rr2
  // Probe on decode_1_rr1
  // Probe on func
  Multiplexer #(.width(5), .enable("false")) multiplexer_1 (
    .in0(decode_1_rr2), .in1(decode_1_out_7), .out(multiplexer_1_out), .sel(RegDst));
  Sign_Extend sign_extend_1 (.in_1(decode_1_out_5), .out_2(sign_extend_1_out_2));
  // Probe on regfile_1_read_data1
  regfile regfile_1 (
    .read_reg1(decode_1_rr1), .read_reg2(decode_1_rr2), .write_register(multiplexer_1_out),
    .write_enable(RegWr), .clock(clock_1_out), .read_data1(regfile_1_read_data1),
    .read_data2(regfile_1_read_data2));  // open: Data, reg_16_val, reg_17_val, reg_18_val, reg_19_val, reg_20_val
  Clock clock_1 (.out(clock_1_out));
  // Probe on sign_extend_1_out_2
  alu alu_1 (
    .Switch(4'b0101), .X(regfile_1_read_data1), .Equal(equal), .Result(alu_1_result),
    .Signed_Overflow_18670403(Signed_OverFlow), .Y(sign_extend_1_out_2));
  // Probe on alu_1_result
  // Probe on memory_data_1_address_2
  // Probe on memory_data_temp_1_address
  memory_data memory_data_1 (
    .Address(alu_1_result), .Write_Data(regfile_1_read_data2), .in_2(clock_2_out), .in_3(MemWr),
    .address_2(memory_data_1_address_2));  // open: Read_Data
  Clock clock_2 (.out(clock_2_out));
  memory_data_temp memory_data_temp_1 (
    .instruction(memory_data_temp_1_instruction), .fetch_addr(alu_1_result),
    .address(memory_data_temp_1_address));
  // Probe on memory_data_temp_1_instruction

  // Notes on the sheet:
  //   rs
  //   rt
  //   op
  //   ALU-Control (5=Add)
  //   Address
  //   Write-Data
endmodule

module Decode (
  input  [31:0] Instruction,
  output [5:0] opcode,
  output [4:0] RR1,
  output [4:0] RR2,
  output [15:0] out_5,
  output [5:0] func,
  output [4:0] out_7
);


  assign func = Instruction[5:0];
  assign opcode = Instruction[31:26];
  assign out_5 = Instruction[15:0];
  assign out_7 = Instruction[15:11];
  assign RR1 = Instruction[25:21];
  assign RR2 = Instruction[20:16];

  // Notes on the sheet:
  //   [26:31]
  //   [21:25]
  //   [16:20]
  //   [0:15]
  //   [0:5]
  //   [11:15]
endmodule

module Sign_Extend (
  input  [15:0] in_1,
  output [31:0] out_2
);

  assign out_2 = {{16{in_1[15]}}, in_1};  // Bit_Extender bit_extender_1
endmodule
